# Fritzing sketch ATX_power_supply_sketch (saved by Fritzing 0.9.3b)

parts:
  J1 = ATX24 Pin Power Supply Connector [package=atx24_right_angle]
  LED2 = smd LED [color="Green (565nm)" package="0603 [SMD]"]
  LED3 = smd LED [color="Yellow (592nm)" package="0603 [SMD]"]
  R1 = Resistor [tolerance=±5% resistance=220 package="0603 [SMD]"]
  R2 = Resistor [tolerance=±5% resistance=220 package="0603 [SMD]"]
  F1 = FUSE [part_number=5A package=fuse_5mm]
  F2 = FUSE [part_number=12A package=fuse_5mm]
  METER1 = 7-Segment Panel Voltmeter
  METER2 = 7-Segment Panel Ammeter
  U1 = SWITCH_SPDT [package=kps-1290]
  X1 = USB Connectors [package=usb-a-s-silk-female]
  S1 = Toggle Switch [package=THT]
  S2 = SPST Switch [package=switch-spst-smd-a]
  JACK1 = 2.1mm Barrel Jack with Terminal Block
  J2 = female pin header, 2 pins [form="♀ (female)"]
  JACK2 = 2.1mm Barrel Jack with Terminal Block
  JACK3 = 2.1mm Barrel Jack with Terminal Block
  JACK4 = 2.1mm Barrel Jack with Terminal Block
  F3 = FUSE [package=fuse_5mm]
  F4 = FUSE [package=fuse_5mm]
  F5 = FUSE [package=fuse_5mm]

nets:
  N1: J1.5V, U1.S
  GND: J1.GND, R1.Pin_1, R2.Pin_1, METER1.V-, METER2.GND, JACK2.NEG, JACK3.NEG, JACK4.NEG
  N2: J1.5V_STDBY, LED3.anode, METER2.V+, F4.2
  N3: J1.12V, F2.1, F5.2
  N4: J1.3.3V, U1.O, F3.2
  N5: J1.PS_ON, S2.P
  N6: LED2.cathode, R2.Pin_0
  N7: LED2.anode, S2.S
  N8: LED3.cathode, R1.Pin_0
  N9: F1.1, U1.P
  N10: F1.2, S1.L2
  N11: F2.2, S1.L1
  N12: METER1.V+, X1.D+, S1.COM, JACK1.POS, J2.pin1
  N13: METER2.LOAD-, X1.GND, JACK1.NEG, J2.pin2
  N14: JACK2.POS, F3.1
  N15: JACK3.POS, F4.1
  N16: JACK4.POS, F5.1

notes:
  Sortie "domino" max 13 A/12V
  Max 5 A 3.3/5/12V

custom parts:
  7-Segment Panel Voltmeter: 7-Segment Panel Voltmeter (4.5 - 30V)
  7-Segment Panel Ammeter: 7-Segment Panel Ammeter (0 to 9.99A)
