# Fritzing sketch ATX_power_supply_sketch_vRelay (saved by Fritzing 0.9.3b)

parts:
  J1 = ATX24 Pin Power Supply Connector [package=atx24_right_angle]
  LED2 = smd LED [color="Green (565nm)" package="0603 [SMD]"]
  LED3 = smd LED [color="Yellow (592nm)" package="0603 [SMD]"]
  R1 = Resistor [tolerance=±5% resistance=220 package="0603 [SMD]"]
  R2 = Resistor [tolerance=±5% resistance=220 package="0603 [SMD]"]
  F1 = FUSE [part_number=5A package=fuse_5mm]
  F2 = FUSE [part_number=12A package=fuse_5mm]
  METER1 = 7-Segment Panel Voltmeter
  METER2 = 7-Segment Panel Ammeter
  X1 = USB Connectors [package=usb-a-s-silk-female]
  S2 = SPST Switch [package=switch-spst-smd-a]
  JACK1 = 2.1mm Barrel Jack with Terminal Block
  J2 = female pin header, 2 pins [form="♀ (female)"]
  JACK2 = 2.1mm Barrel Jack with Terminal Block
  JACK3 = 2.1mm Barrel Jack with Terminal Block
  JACK4 = 2.1mm Barrel Jack with Terminal Block
  F3 = FUSE [package=fuse_5mm]
  F4 = FUSE [package=fuse_5mm]
  F5 = FUSE [package=fuse_5mm]
  U3 = RELAY [package=relay-g5q]
  switch1 = Rotary_Switch_12x1
  U4 = RELAY [package=relay-g5q]

nets:
  GND: J1.GND, R1.Pin_1, R2.Pin_1, METER1.V-, METER2.GND, JACK2.NEG, JACK3.NEG, JACK4.NEG, U3.COIL2, U4.COIL2
  N1: J1.5V, U4.NO
  N2: J1.5V_STDBY, LED3.anode, METER2.V+, F4.2
  N3: J1.12V, F2.1, F5.2
  N4: J1.3.3V, F3.2, switch1.0, U4.NC
  N5: J1.PS_ON, S2.P
  N6: LED2.cathode, R2.Pin_0
  N7: LED2.anode, S2.S
  N8: LED3.cathode, R1.Pin_0
  N9: F1.1, U4.MAIN
  N10: F1.2, U3.NC
  N11: F2.2, U3.NO
  N12: METER1.V+, X1.VBUS, JACK1.POS, J2.pin1, U3.MAIN
  N13: METER2.LOAD-, X1.GND, JACK1.NEG, J2.pin2
  N14: JACK2.POS, F3.1
  N15: JACK3.POS, F4.1
  N16: JACK4.POS, F5.1
  N17: U3.COIL1, switch1.5
  N18: switch1.6, U4.COIL1

notes:
  Sortie "domino" max 13 A/12V
  Max 5 A 3.3/5/12V
  Rotary at least 3T. Voltage selection trigger 3.3/5 V or 12V relay
  or trigger 3.3 or 12V
  Rather banana plugs
  Relay 3.3V . R = 66.1 Ohms
  I = 50 mA

custom parts:
  7-Segment Panel Voltmeter: 7-Segment Panel Voltmeter (4.5 - 30V)
  7-Segment Panel Ammeter: 7-Segment Panel Ammeter (0 to 9.99A)
